// Logisim project Pre-Lab_8_batinayunsel_20070001051.circ as structural Verilog
module halfadder (
  input  A,
  input  B,
  output S,
  output C
);

  xor xor_1 (S, A, B);
  and and_1 (C, A, B);
endmodule

module fulladder (
  input  Cin,
  input  A,
  input  B,
  output S,
  output C
);

  wire and_1_out, and_2_out, halfadder_1_c, halfadder_1_s;

  halfadder halfadder_1 (.A(A), .B(B), .S(halfadder_1_s), .C(halfadder_1_c));
  and and_1 (and_1_out, Cin, A);
  and and_2 (and_2_out, Cin, B);
  xor xor_1 (S, Cin, halfadder_1_s);
  or or_1 (C, halfadder_1_c, and_1_out, and_2_out);
endmodule

module _8bitaddercircuit (
  input  [7:0] A,
  input  [7:0] B,
  output [7:0] _8_Out,
  output C
);

  wire fulladder_1_c, fulladder_2_c, fulladder_3_c, fulladder_4_c, fulladder_5_c, fulladder_6_c,
       halfadder_1_c;

  halfadder halfadder_1 (.A(A[0]), .B(B[0]), .S(_8_Out[0]), .C(halfadder_1_c));
  fulladder fulladder_1 (.Cin(halfadder_1_c), .A(A[1]), .B(B[1]), .S(_8_Out[1]), .C(fulladder_1_c));
  fulladder fulladder_2 (.Cin(fulladder_1_c), .A(A[2]), .B(B[2]), .S(_8_Out[2]), .C(fulladder_2_c));
  fulladder fulladder_3 (.Cin(fulladder_2_c), .A(A[3]), .B(B[3]), .S(_8_Out[3]), .C(fulladder_3_c));
  fulladder fulladder_4 (.Cin(fulladder_3_c), .A(A[4]), .B(B[4]), .S(_8_Out[4]), .C(fulladder_4_c));
  fulladder fulladder_5 (.Cin(fulladder_4_c), .A(A[5]), .B(B[5]), .S(_8_Out[5]), .C(fulladder_5_c));
  fulladder fulladder_6 (.Cin(fulladder_5_c), .A(A[6]), .B(B[6]), .S(_8_Out[6]), .C(fulladder_6_c));
  fulladder fulladder_7 (.Cin(fulladder_6_c), .A(A[7]), .B(B[7]), .S(_8_Out[7]), .C(C));
endmodule
