// Logisim project batinayunsel_20070001051_lab11.circ as structural Verilog
// register file
module RegisterFile (
  input  [2:0] WRITE_ADDRESS,
  input  WEN,
  input  CLOCK,
  input  [7:0] writedata,
  input  [2:0] READ_ADDRESS1,
  input  [2:0] READ_ADDRESS2,
  output [7:0] A,
  output [7:0] B
);

  wire and_1_out, and_2_out, and_3_out, and_4_out, and_5_out, and_6_out, and_7_out, and_8_out,
       decoder_1_out0, decoder_1_out1, decoder_1_out2, decoder_1_out3, decoder_1_out4, decoder_1_out5,
       decoder_1_out6, decoder_1_out7;
  wire [7:0] n8bitreg_1_output_to_reg, n8bitreg_2_output_to_reg, n8bitreg_3_output_to_reg,
       n8bitreg_4_output_to_reg, n8bitreg_5_output_to_reg, n8bitreg_6_output_to_reg,
       n8bitreg_7_output_to_reg, n8bitreg_8_output_to_reg;

  and and_1 (and_1_out, WEN, decoder_1_out0);
  and and_2 (and_2_out, WEN, decoder_1_out1);
  and and_3 (and_3_out, WEN, decoder_1_out2);
  and and_4 (and_4_out, WEN, decoder_1_out3);
  and and_5 (and_5_out, WEN, decoder_1_out4);
  and and_6 (and_6_out, WEN, decoder_1_out5);
  and and_7 (and_7_out, WEN, decoder_1_out6);
  and and_8 (and_8_out, WEN, decoder_1_out7);
  _8bitreg u_8bitreg_1 (
    .inputto_Reg(writedata), .Clock(CLOCK), .Enable_from_Dec(and_1_out),
    .Output_to_Reg(n8bitreg_1_output_to_reg));
  _8bitreg u_8bitreg_2 (
    .inputto_Reg(writedata), .Clock(CLOCK), .Enable_from_Dec(and_2_out),
    .Output_to_Reg(n8bitreg_2_output_to_reg));
  _8bitreg u_8bitreg_3 (
    .inputto_Reg(writedata), .Clock(CLOCK), .Enable_from_Dec(and_3_out),
    .Output_to_Reg(n8bitreg_3_output_to_reg));
  _8bitreg u_8bitreg_4 (
    .inputto_Reg(writedata), .Clock(CLOCK), .Enable_from_Dec(and_4_out),
    .Output_to_Reg(n8bitreg_4_output_to_reg));
  _8bitreg u_8bitreg_5 (
    .inputto_Reg(writedata), .Clock(CLOCK), .Enable_from_Dec(and_5_out),
    .Output_to_Reg(n8bitreg_5_output_to_reg));
  _8bitreg u_8bitreg_6 (
    .inputto_Reg(writedata), .Clock(CLOCK), .Enable_from_Dec(and_6_out),
    .Output_to_Reg(n8bitreg_6_output_to_reg));
  _8bitreg u_8bitreg_7 (
    .inputto_Reg(writedata), .Clock(CLOCK), .Enable_from_Dec(and_7_out),
    .Output_to_Reg(n8bitreg_7_output_to_reg));
  _8bitreg u_8bitreg_8 (
    .inputto_Reg(writedata), .Clock(CLOCK), .Enable_from_Dec(and_8_out),
    .Output_to_Reg(n8bitreg_8_output_to_reg));
  Decoder #(.select(3)) decoder_1 (
    .out0(decoder_1_out0), .out1(decoder_1_out1), .out2(decoder_1_out2), .out3(decoder_1_out3),
    .out4(decoder_1_out4), .out5(decoder_1_out5), .out6(decoder_1_out6), .out7(decoder_1_out7),
    .sel(WRITE_ADDRESS));  // open: en
  Multiplexer #(.select(3), .width(8)) multiplexer_1 (
    .in0(n8bitreg_1_output_to_reg), .in1(n8bitreg_2_output_to_reg), .in2(n8bitreg_3_output_to_reg),
    .in3(n8bitreg_4_output_to_reg), .in4(n8bitreg_5_output_to_reg), .in5(n8bitreg_6_output_to_reg),
    .in6(n8bitreg_7_output_to_reg), .in7(n8bitreg_8_output_to_reg), .out(A), .sel(READ_ADDRESS1));  // open: en
  Multiplexer #(.select(3), .width(8)) multiplexer_2 (
    .in0(n8bitreg_1_output_to_reg), .in1(n8bitreg_2_output_to_reg), .in2(n8bitreg_3_output_to_reg),
    .in3(n8bitreg_4_output_to_reg), .in4(n8bitreg_5_output_to_reg), .in5(n8bitreg_6_output_to_reg),
    .in6(n8bitreg_7_output_to_reg), .in7(n8bitreg_8_output_to_reg), .out(B), .sel(READ_ADDRESS2));  // open: en
endmodule

module _8bitreg (
  input  Clock,
  input  Enable_from_Dec,
  input  [7:0] inputto_Reg,
  output [7:0] Output_to_Reg
);

  D_Flip_Flop d_ff_1 (
    .clk(Clock), .D(inputto_Reg[0]), .Q(Output_to_Reg[0]), .en(Enable_from_Dec));  // open: Qn, preset, reset
  D_Flip_Flop d_ff_2 (
    .clk(Clock), .D(inputto_Reg[1]), .Q(Output_to_Reg[1]), .en(Enable_from_Dec));  // open: Qn, preset, reset
  D_Flip_Flop d_ff_3 (
    .clk(Clock), .D(inputto_Reg[2]), .Q(Output_to_Reg[2]), .en(Enable_from_Dec));  // open: Qn, preset, reset
  D_Flip_Flop d_ff_4 (
    .clk(Clock), .D(inputto_Reg[3]), .Q(Output_to_Reg[3]), .en(Enable_from_Dec));  // open: Qn, preset, reset
  D_Flip_Flop d_ff_5 (
    .clk(Clock), .D(inputto_Reg[4]), .Q(Output_to_Reg[4]), .en(Enable_from_Dec));  // open: Qn, preset, reset
  D_Flip_Flop d_ff_6 (
    .clk(Clock), .D(inputto_Reg[5]), .Q(Output_to_Reg[5]), .en(Enable_from_Dec));  // open: Qn, preset, reset
  D_Flip_Flop d_ff_7 (
    .clk(Clock), .D(inputto_Reg[6]), .Q(Output_to_Reg[6]), .en(Enable_from_Dec));  // open: Qn, preset, reset
  D_Flip_Flop d_ff_8 (
    .clk(Clock), .D(inputto_Reg[7]), .Q(Output_to_Reg[7]), .en(Enable_from_Dec));  // open: Qn, preset, reset
endmodule

module TestRegFile (
  input  [7:0] inputto_Reg,
  input  [2:0] WRITE_ADDRESS,
  input  WEN,
  input  [2:0] READ_ADDRESS1,
  input  [2:0] READ_ADDRESS2,
  input  [2:0] OPCODE,
  output [7:0] A,
  output [7:0] B,
  output [7:0] RESULT,
  output out_10
);

  wire CLOCK_out;

  Clock CLOCK (.out(CLOCK_out));
  RegisterFile registerfile_1 (
    .WRITE_ADDRESS(WRITE_ADDRESS), .WEN(WEN), .CLOCK(CLOCK_out), .writedata(inputto_Reg),
    .READ_ADDRESS1(READ_ADDRESS2), .READ_ADDRESS2(READ_ADDRESS1), .A(A), .B(B));
  _1_bit_alu u_1_bit_alu_1 (.A(A), .B(B), .opcode(OPCODE), .RESULT(RESULT), .ZERO(out_10));
endmodule

// alu
module _1_bit_alu (
  input  [7:0] A,
  input  [7:0] B,
  input  [2:0] opcode,
  output [7:0] RESULT,
  output ZERO
);

  wire comparator_1_lt;
  wire [7:0] adder_1_out, and_1_out, not_1_out, or_1_out, SLT, subtractor_1_out, xnor_1_out, xor_1_out;

  Comparator comparator_1 (.a(B), .b(A), .lt(comparator_1_lt));  // open: gt, eq
  assign SLT = {{7{1'b0}}, comparator_1_lt};  // Bit_Extender bit_extender_1
  assign and_1_out = A & B;  // AND_Gate and_1, 8 bits wide
  assign or_1_out = A | B;  // OR_Gate or_1, 8 bits wide
  Adder adder_1 (.a(A), .b(B), .out(adder_1_out));  // open: cin, cout
  Subtractor subtractor_1 (.a(A), .b(B), .out(subtractor_1_out));  // open: bin, bout
  assign xor_1_out = A ^ B;  // XOR_Gate xor_1, 8 bits wide
  assign xnor_1_out = ~(A ^ B);  // XNOR_Gate xnor_1, 8 bits wide
  assign not_1_out = ~or_1_out;  // NOT_Gate not_1, 8 bits wide
  Multiplexer #(.select(3), .width(8)) multiplexer_1 (
    .in0(and_1_out), .in1(or_1_out), .in2(adder_1_out), .in3(subtractor_1_out), .in4(SLT), .in5(xor_1_out),
    .in6(xnor_1_out), .in7(not_1_out), .out(RESULT), .sel(opcode));  // open: en
  nor nor_1 (ZERO, RESULT[0], RESULT[1], RESULT[2], RESULT[3], RESULT[4], RESULT[5], RESULT[6], RESULT[7]);
endmodule

module singlecycle (
  output [7:0] out_1
);

  wire and_1_out, CLK, control_unit_1_alusrc, control_unit_1_branch, control_unit_1_jump,
       control_unit_1_memtoread, control_unit_1_memtoreg, control_unit_1_memtowrite, control_unit_1_regdst,
       control_unit_1_regwrite, n1_bit_alu_1_zero, not_1_out;
  wire [1:0] control_unit_1_alu_1;
  wire [2:0] alu_control_1_out_3, multiplexer_1_out;
  wire [7:0] adder_1_out, adder_2_out, multiplexer_2_out, multiplexer_3_out, multiplexer_4_out,
       multiplexer_5_out, PC_q, ram_1_data, registerfile_1_a, registerfile_1_b;
  wire [17:0] rom_1_data;

  Clock clock_1 (.out(CLK));
  Register PC (.D(multiplexer_4_out), .Q(PC_q), .clk(CLK));  // open: en, clr
  Adder adder_1 (.a(PC_q), .b(8'h1), .out(adder_1_out));  // open: cin, cout
  control_unit control_unit_1 (
    .in_1(rom_1_data[17:14]), .RegdST(control_unit_1_regdst), .jump(control_unit_1_jump),
    .branch(control_unit_1_branch), .memtoread(control_unit_1_memtoread), .memtoreg(control_unit_1_memtoreg),
    .alu_1(control_unit_1_alu_1[0]), .alu_2(control_unit_1_alu_1[1]), .memtowrite(control_unit_1_memtowrite),
    .AluSRC(control_unit_1_alusrc), .RegWrite(control_unit_1_regwrite));
  ROM #(.dataWidth(18)) rom_1 (.addr(PC_q), .data(rom_1_data));  // open: sel
  Multiplexer #(.width(3), .enable("false")) multiplexer_1 (
    .in0(rom_1_data[10:8]), .in1(rom_1_data[7:5]), .out(multiplexer_1_out), .sel(control_unit_1_regdst));
  RegisterFile registerfile_1 (
    .WRITE_ADDRESS(multiplexer_1_out), .WEN(control_unit_1_regwrite), .CLOCK(CLK),
    .writedata(multiplexer_5_out), .READ_ADDRESS1(rom_1_data[13:11]), .READ_ADDRESS2(rom_1_data[10:8]),
    .A(registerfile_1_a), .B(registerfile_1_b));
  Multiplexer #(.width(8), .enable("false")) multiplexer_2 (
    .in0(registerfile_1_b), .in1(rom_1_data[7:0]), .out(multiplexer_2_out), .sel(control_unit_1_alusrc));
  Adder adder_2 (.a(adder_1_out), .b(registerfile_1_b), .out(adder_2_out));  // open: cin, cout
  _1_bit_alu u_1_bit_alu_1 (
    .A(registerfile_1_a), .B(multiplexer_2_out), .opcode(alu_control_1_out_3), .RESULT(out_1),
    .ZERO(n1_bit_alu_1_zero));
  alu_control alu_control_1 (.alu_op(control_unit_1_alu_1), .\ınstrcton (rom_1_data[2:0]), .out_3(alu_control_1_out_3));
  and and_1 (and_1_out, control_unit_1_branch, n1_bit_alu_1_zero);
  Multiplexer #(.width(8), .enable("false")) multiplexer_3 (
    .in0(adder_1_out), .in1(adder_2_out), .out(multiplexer_3_out), .sel(and_1_out));
  not not_1 (not_1_out, CLK);
  Multiplexer #(.width(8), .enable("false")) multiplexer_4 (
    .in0(multiplexer_3_out), .in1(registerfile_1_b), .out(multiplexer_4_out), .sel(control_unit_1_jump));
  RAM #(.bus("separate")) ram_1 (
    .addr(out_1), .din(registerfile_1_b), .data(ram_1_data), .str(control_unit_1_memtowrite),
    .clk(not_1_out), .ld(control_unit_1_memtoread));  // open: sel, clr
  Multiplexer #(.width(8), .enable("false")) multiplexer_5 (
    .in0(out_1), .in1(ram_1_data), .out(multiplexer_5_out), .sel(control_unit_1_memtoreg));

  // Notes on the sheet:
  //   contents of rom_1 (hex, n*v repeats v):
  //   20000 2010e 2021a a60 a81 aa2 ac3 ae5 2c000 2c101 2c202 2c303 2c404 2c505 2c606 2c707
endmodule

// control
module control_unit (
  input  [3:0] in_1,
  output RegdST,
  output jump,
  output branch,
  output memtoread,
  output memtoreg,
  output alu_1,
  output alu_2,
  output memtowrite,
  output AluSRC,
  output RegWrite
);

  wire decoder_1_out8;

  Decoder #(.select(4), .enable("false")) decoder_1 (
    .out0(alu_2), .out2(jump), .out3(memtoread), .out4(alu_1), .out8(decoder_1_out8), .out11(memtowrite),
    .sel(in_1));  // open: out1, out5, out6, out7, out9, out10, out12, out13, out14, out15
  or or_1 (AluSRC, memtowrite, decoder_1_out8, memtoread);
  or or_2 (RegWrite, alu_2, memtoread, decoder_1_out8);

  assign branch = alu_1;
  assign memtoreg = memtoread;
  assign RegdST = alu_2;
endmodule

module alu_control (
  input  [1:0] alu_op,
  input  [2:0] \ınstrcton ,
  output [2:0] out_3
);

  wire and_1_out, not_1_out;

  and and_1 (and_1_out, \ınstrcton [0], alu_op[1]);
  and and_2 (out_3[2], alu_op[1], \ınstrcton [2]);
  not not_1 (not_1_out, alu_op[1]);
  or or_1 (out_3[0], alu_op[0], and_1_out);
  or or_2 (out_3[1], not_1_out, \ınstrcton [1]);
endmodule
