// Logisim project lab8batinayunsel_20070001051.circ as structural Verilog
module RegisterFile (
  input  [2:0] WRITE_ADDRESS,
  input  WEN,
  input  CLOCK,
  input  [7:0] inputto_Reg,
  input  [2:0] READ_ADDRESS1,
  input  [2:0] READ_ADDRESS2,
  output [7:0] A,
  output [7:0] B
);

  wire and_1_out, and_2_out, and_3_out, and_4_out, and_5_out, and_6_out, and_7_out, and_8_out,
       decoder_1_out0, decoder_1_out1, decoder_1_out2, decoder_1_out3, decoder_1_out4, decoder_1_out5,
       decoder_1_out6, decoder_1_out7;
  wire [7:0] n8bitreg_1_output_to_reg, n8bitreg_2_output_to_reg, n8bitreg_3_output_to_reg,
       n8bitreg_4_output_to_reg, n8bitreg_5_output_to_reg, n8bitreg_6_output_to_reg,
       n8bitreg_7_output_to_reg, n8bitreg_8_output_to_reg;

  and and_1 (and_1_out, WEN, decoder_1_out0);
  and and_2 (and_2_out, WEN, decoder_1_out1);
  and and_3 (and_3_out, WEN, decoder_1_out2);
  and and_4 (and_4_out, WEN, decoder_1_out3);
  and and_5 (and_5_out, WEN, decoder_1_out4);
  and and_6 (and_6_out, WEN, decoder_1_out5);
  and and_7 (and_7_out, WEN, decoder_1_out6);
  and and_8 (and_8_out, WEN, decoder_1_out7);
  _8bitreg u_8bitreg_1 (
    .inputto_Reg(inputto_Reg), .Clock(CLOCK), .Enable_from_Dec(and_1_out),
    .Output_to_Reg(n8bitreg_1_output_to_reg));
  _8bitreg u_8bitreg_2 (
    .inputto_Reg(inputto_Reg), .Clock(CLOCK), .Enable_from_Dec(and_2_out),
    .Output_to_Reg(n8bitreg_2_output_to_reg));
  _8bitreg u_8bitreg_3 (
    .inputto_Reg(inputto_Reg), .Clock(CLOCK), .Enable_from_Dec(and_3_out),
    .Output_to_Reg(n8bitreg_3_output_to_reg));
  _8bitreg u_8bitreg_4 (
    .inputto_Reg(inputto_Reg), .Clock(CLOCK), .Enable_from_Dec(and_4_out),
    .Output_to_Reg(n8bitreg_4_output_to_reg));
  _8bitreg u_8bitreg_5 (
    .inputto_Reg(inputto_Reg), .Clock(CLOCK), .Enable_from_Dec(and_5_out),
    .Output_to_Reg(n8bitreg_5_output_to_reg));
  _8bitreg u_8bitreg_6 (
    .inputto_Reg(inputto_Reg), .Clock(CLOCK), .Enable_from_Dec(and_6_out),
    .Output_to_Reg(n8bitreg_6_output_to_reg));
  _8bitreg u_8bitreg_7 (
    .inputto_Reg(inputto_Reg), .Clock(CLOCK), .Enable_from_Dec(and_7_out),
    .Output_to_Reg(n8bitreg_7_output_to_reg));
  _8bitreg u_8bitreg_8 (
    .inputto_Reg(inputto_Reg), .Clock(CLOCK), .Enable_from_Dec(and_8_out),
    .Output_to_Reg(n8bitreg_8_output_to_reg));
  Decoder #(.select(3)) decoder_1 (
    .out0(decoder_1_out0), .out1(decoder_1_out1), .out2(decoder_1_out2), .out3(decoder_1_out3),
    .out4(decoder_1_out4), .out5(decoder_1_out5), .out6(decoder_1_out6), .out7(decoder_1_out7),
    .sel(WRITE_ADDRESS));  // open: en
  Multiplexer #(.select(3), .width(8)) multiplexer_1 (
    .in0(n8bitreg_1_output_to_reg), .in1(n8bitreg_2_output_to_reg), .in2(n8bitreg_3_output_to_reg),
    .in3(n8bitreg_4_output_to_reg), .in4(n8bitreg_5_output_to_reg), .in5(n8bitreg_6_output_to_reg),
    .in6(n8bitreg_7_output_to_reg), .in7(n8bitreg_8_output_to_reg), .out(A), .sel(READ_ADDRESS1));  // open: en
  Multiplexer #(.select(3), .width(8)) multiplexer_2 (
    .in0(n8bitreg_1_output_to_reg), .in1(n8bitreg_2_output_to_reg), .in2(n8bitreg_3_output_to_reg),
    .in3(n8bitreg_4_output_to_reg), .in4(n8bitreg_5_output_to_reg), .in5(n8bitreg_6_output_to_reg),
    .in6(n8bitreg_7_output_to_reg), .in7(n8bitreg_8_output_to_reg), .out(B), .sel(READ_ADDRESS2));  // open: en
endmodule

module _8bitreg (
  input  Clock,
  input  Enable_from_Dec,
  input  [7:0] inputto_Reg,
  output [7:0] Output_to_Reg
);

  D_Flip_Flop d_ff_1 (
    .clk(Clock), .D(inputto_Reg[0]), .Q(Output_to_Reg[0]), .en(Enable_from_Dec));  // open: Qn, preset, reset
  D_Flip_Flop d_ff_2 (
    .clk(Clock), .D(inputto_Reg[1]), .Q(Output_to_Reg[1]), .en(Enable_from_Dec));  // open: Qn, preset, reset
  D_Flip_Flop d_ff_3 (
    .clk(Clock), .D(inputto_Reg[2]), .Q(Output_to_Reg[2]), .en(Enable_from_Dec));  // open: Qn, preset, reset
  D_Flip_Flop d_ff_4 (
    .clk(Clock), .D(inputto_Reg[3]), .Q(Output_to_Reg[3]), .en(Enable_from_Dec));  // open: Qn, preset, reset
  D_Flip_Flop d_ff_5 (
    .clk(Clock), .D(inputto_Reg[4]), .Q(Output_to_Reg[4]), .en(Enable_from_Dec));  // open: Qn, preset, reset
  D_Flip_Flop d_ff_6 (
    .clk(Clock), .D(inputto_Reg[5]), .Q(Output_to_Reg[5]), .en(Enable_from_Dec));  // open: Qn, preset, reset
  D_Flip_Flop d_ff_7 (
    .clk(Clock), .D(inputto_Reg[6]), .Q(Output_to_Reg[6]), .en(Enable_from_Dec));  // open: Qn, preset, reset
  D_Flip_Flop d_ff_8 (
    .clk(Clock), .D(inputto_Reg[7]), .Q(Output_to_Reg[7]), .en(Enable_from_Dec));  // open: Qn, preset, reset
endmodule

module TestRegFile (
  input  [7:0] inputto_Reg,
  input  [2:0] WRITE_ADDRESS,
  input  WEN,
  input  [2:0] READ_ADDRESS1,
  input  [2:0] READ_ADDRESS2,
  input  [2:0] OPCODE,
  output [7:0] A,
  output [7:0] B,
  output [7:0] RESULT,
  output out_10
);

  wire CLOCK_out;

  Clock CLOCK (.out(CLOCK_out));
  RegisterFile registerfile_1 (
    .WRITE_ADDRESS(WRITE_ADDRESS), .WEN(WEN), .CLOCK(CLOCK_out), .inputto_Reg(inputto_Reg),
    .READ_ADDRESS1(READ_ADDRESS2), .READ_ADDRESS2(READ_ADDRESS1), .A(A), .B(B));
  _1_bit_alu u_1_bit_alu_1 (.A(A), .B(B), .opcode(OPCODE), .RESULT(RESULT), .ZERO(out_10));
endmodule

module _1_bit_alu (
  input  [7:0] A,
  input  [7:0] B,
  input  [2:0] opcode,
  output [7:0] RESULT,
  output ZERO
);

  wire comparator_1_lt;
  wire [7:0] adder_1_out, and_1_out, not_1_out, or_1_out, SLT, subtractor_1_out, xnor_1_out, xor_1_out;

  Comparator comparator_1 (.a(B), .b(A), .lt(comparator_1_lt));  // open: gt, eq
  assign SLT = {{7{1'b0}}, comparator_1_lt};  // Bit_Extender bit_extender_1
  assign and_1_out = A & B;  // AND_Gate and_1, 8 bits wide
  assign or_1_out = A | B;  // OR_Gate or_1, 8 bits wide
  Adder adder_1 (.a(A), .b(B), .out(adder_1_out));  // open: cin, cout
  Subtractor subtractor_1 (.a(A), .b(B), .out(subtractor_1_out));  // open: bin, bout
  assign xor_1_out = A ^ B;  // XOR_Gate xor_1, 8 bits wide
  assign xnor_1_out = ~(A ^ B);  // XNOR_Gate xnor_1, 8 bits wide
  assign not_1_out = ~or_1_out;  // NOT_Gate not_1, 8 bits wide
  Multiplexer #(.select(3), .width(8)) multiplexer_1 (
    .in0(and_1_out), .in1(or_1_out), .in2(adder_1_out), .in3(subtractor_1_out), .in4(SLT), .in5(xor_1_out),
    .in6(xnor_1_out), .in7(not_1_out), .out(RESULT), .sel(opcode));  // open: en
  nor nor_1 (ZERO, RESULT[0], RESULT[1], RESULT[2], RESULT[3], RESULT[4], RESULT[5], RESULT[6], RESULT[7]);
endmodule
